# Fritzing sketch bb_beerPongGame (saved by Fritzing 0.9.4)
breadboards: 1

parts:
  Q1 = PHOTOTRANSISTOR REFLECTIVE OBJECT SENSOR [package=qrb1114-side]
  Q2 = PHOTOTRANSISTOR REFLECTIVE OBJECT SENSOR [package=qrb1114-side]
  Q3 = PHOTOTRANSISTOR REFLECTIVE OBJECT SENSOR [package=qrb1114-side]
  Q4 = PHOTOTRANSISTOR REFLECTIVE OBJECT SENSOR [package=qrb1114-side]
  Q5 = PHOTOTRANSISTOR REFLECTIVE OBJECT SENSOR [package=qrb1114-side]
  Q6 = PHOTOTRANSISTOR REFLECTIVE OBJECT SENSOR [package=qrb1114-side]
  R1 = Resistor [tolerance=±5% resistance=10k package="2010 [SMD]"]
  R2 = Resistor [tolerance=±5% resistance=10k package="2010 [SMD]"]
  R3 = Resistor [tolerance=±5% resistance=10k package="2010 [SMD]"]
  R4 = Resistor [tolerance=±5% resistance=10k package="2010 [SMD]"]
  R6 = Resistor [tolerance=±5% resistance=10k package="2010 [SMD]"]
  R7 = Resistor [tolerance=±5% resistance=10k package="2010 [SMD]"]
  R8 = Resistor [tolerance=±5% resistance=470 package="2010 [SMD]"]
  R9 = Resistor [tolerance=±5% resistance=470 package="2010 [SMD]"]
  R10 = Resistor [tolerance=±5% resistance=470 package="2010 [SMD]"]
  R11 = Resistor [tolerance=±5% resistance=470 package="2010 [SMD]"]
  R12 = Resistor [tolerance=±5% resistance=470 package="2010 [SMD]"]
  R13 = Resistor [tolerance=±5% resistance=470 package="2010 [SMD]"]
  Part1 = Itsy Bitsy 32u4 5V @ 16MHz [part_number="Adafruit #3677"]

nets:
  N1: Q1.A, R13.Pin_0
  N2: Q1.C, R2.Pin_0, Part1.A1
  N3: Q1.E, Q1.K, Q2.E, Q2.K, Q3.E, Q3.K, Q4.E, Q4.K, Q5.E, Q5.K, Q6.E, Q6.K, Part1.GND
  N4: Q2.A, R12.Pin_0
  N5: Q2.C, R3.Pin_0, Part1.A2
  N6: Q3.A, R11.Pin_0
  N7: Q3.C, R4.Pin_0, Part1.A3
  N8: Q4.A, R10.Pin_0
  N9: Q4.C, R1.Pin_0, Part1.A5
  N10: Q5.A, R9.Pin_0
  N11: Q5.C, R7.Pin_0, Part1.A4
  N12: Q6.A, R8.Pin_0
  N13: Q6.C, R6.Pin_0, Part1.A0
  N14: R1.Pin_1, R2.Pin_1, R3.Pin_1, R4.Pin_1, R6.Pin_1, R7.Pin_1, Part1.+5V
  N15: R8.Pin_1, Part1.D13
  N16: R9.Pin_1, Part1.D8
  N17: R10.Pin_1, Part1.D6
  N18: R11.Pin_1, Part1.D10
  N19: R12.Pin_1, Part1.D11
  N20: R13.Pin_1, Part1.D12

custom parts:
  Itsy Bitsy 32u4 5V @ 16MHz: What's smaller than a Feather but larger than a Trinket? It's an Itsy Bitsy! Small, powerful, Arduino-compatible - this microcontroller board is perfect when you want something very compact, but still with a bunch of pins. Itsy Bitsy is only 1.4" long by 0.7" wide, but has 6 power pins, 6 analog & digital pins and 17 digital pins. It packs much of the same capability as an Arduino UNO. So it's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
